// Logisim project digital1.circ as structural Verilog: 1 circuit, main circuit main
module main (
);

  wire dipswitch_1_sw1, dipswitch_1_sw2, dipswitch_3_sw1, dipswitch_3_sw2, n7420_1_pin1, n7420_1_pin2,
       n7420_1_pin4, n7420_1_pin5, n7420_1_pin6, n7486_1_pin3, n74125_1_pin3;

  DipSwitch dipswitch_1 (.sw1(dipswitch_1_sw1), .sw2(dipswitch_1_sw2));  // open: sw3, sw4, sw5, sw6, sw7, sw8
  _7486 u_7486_1 (
    .pin1(dipswitch_1_sw1), .pin2(dipswitch_1_sw2), .pin3(n7486_1_pin3));  // open: pin4, pin5, pin6, pin13, pin12, pin11, pin10, pin9, pin8
  LED led_1 (.in(n7486_1_pin3));
  _7420 u_7420_1 (
    .pin1(n7420_1_pin1), .pin2(n7420_1_pin2), .pin4(n7420_1_pin4), .pin5(n7420_1_pin5), .pin6(n7420_1_pin6));  // open: pin3, pin13, pin12, pin11, pin10, pin9, pin8
  DipSwitch dipswitch_2 (
    .sw1(n7420_1_pin1), .sw2(n7420_1_pin2), .sw3(n7420_1_pin4), .sw4(n7420_1_pin5));  // open: sw5, sw6, sw7, sw8
  LED led_2 (.in(n7420_1_pin6));
  DipSwitch dipswitch_3 (.sw1(dipswitch_3_sw1), .sw2(dipswitch_3_sw2));  // open: sw3, sw4, sw5, sw6, sw7, sw8
  _74125 u_74125_1 (
    .pin1(dipswitch_3_sw1), .pin2(dipswitch_3_sw2), .pin3(n74125_1_pin3));  // open: pin4, pin5, pin6, pin13, pin12, pin11, pin10, pin9, pin8
  LED led_3 (.in(n74125_1_pin3));
endmodule
