// Logisim project digital2.circ as structural Verilog: 1 circuit, main circuit main
module main (
);

  wire dipswitch_1_sw1, n7400_1_pin1, n7400_1_pin2, n7400_1_pin3, n7400_1_pin5, n7400_1_pin6, n7400_2_pin1,
       n7400_2_pin2, n7400_2_pin3, n7404_1_pin5, n7404_1_pin6, n7404_1_pin7, n7404_1_pin14, n7404_2_pin7,
       n7404_2_pin12, n7404_2_pin14, n7420_1_pin6, n7420_2_pin6, n7432_1_pin3, n7485_1_pin1, n7485_1_pin3,
       n7485_1_pin5, n7485_1_pin6, n7485_1_pin7, n7485_1_pin10, n7485_1_pin12, n7485_1_pin13, n7485_1_pin15,
       n74138_1_pin1, n74138_1_pin2, n74138_1_pin3, n74138_1_pin7, n74138_1_pin9, n74138_1_pin10,
       n74151_1_pin1, n74151_1_pin5, n74151_1_pin9, n74151_1_pin10, n74151_1_pin11, not_1_out;

  _7404 #(.VccGndPorts("true")) u_7404_1 (
    .pin5(n7404_1_pin5), .pin6(n7404_1_pin6), .pin7(n7404_1_pin7), .pin14(n7404_1_pin14));  // open: pin1, pin2, pin3, pin4, pin13, pin12, pin11, pin10, pin9, pin8
  _74138 #(.VccGndPorts("true")) u_74138_1 (
    .pin1(n74138_1_pin1), .pin2(n74138_1_pin2), .pin3(n74138_1_pin3), .pin4(n7404_1_pin5),
    .pin5(n7404_1_pin5), .pin6(n7404_1_pin6), .pin7(n74138_1_pin7), .pin8(n7404_1_pin7),
    .pin16(n7404_1_pin14), .pin10(n74138_1_pin10), .pin9(n74138_1_pin9));  // open: pin15, pin14, pin13, pin12, pin11
  _7400 u_7400_1 (
    .pin1(n7400_1_pin1), .pin2(n7400_1_pin2), .pin3(n7400_1_pin3), .pin4(n7400_1_pin1), .pin5(n7400_1_pin5),
    .pin6(n7400_1_pin6));  // open: pin13, pin12, pin11, pin10, pin9, pin8
  DipSwitch dipswitch_1 (
    .sw1(dipswitch_1_sw1), .sw2(n7400_1_pin1), .sw3(n7400_1_pin5), .sw4(n7400_1_pin2));  // open: sw5, sw6, sw7, sw8
  not not_1 (not_1_out, n74151_1_pin1);
  _74151 #(.VccGndPorts("true")) u_74151_1 (
    .pin1(n74151_1_pin1), .pin2(n74151_1_pin1), .pin3(n74151_1_pin1), .pin4(n74151_1_pin1),
    .pin5(n74151_1_pin5), .pin7(n74151_1_pin1), .pin8(n74151_1_pin1), .pin16(not_1_out),
    .pin15(n74151_1_pin1), .pin14(not_1_out), .pin13(not_1_out), .pin12(not_1_out), .pin11(n74151_1_pin11),
    .pin10(n74151_1_pin10), .pin9(n74151_1_pin9));  // open: pin6
  _7420 #(.VccGndPorts("true")) u_7420_1 (
    .pin1(n74138_1_pin10), .pin2(n74138_1_pin9), .pin4(n74138_1_pin7), .pin5(n7404_1_pin14),
    .pin6(n7420_1_pin6), .pin7(n7404_1_pin7), .pin14(n7404_1_pin14));  // open: pin3, pin13, pin12, pin11, pin10, pin9, pin8
  _7485 #(.VccGndPorts("true")) u_7485_1 (
    .pin1(n7485_1_pin1), .pin2(n7485_1_pin1), .pin3(n7485_1_pin3), .pin4(n7485_1_pin1), .pin5(n7485_1_pin5),
    .pin6(n7485_1_pin6), .pin7(n7485_1_pin7), .pin8(n7485_1_pin1), .pin16(n7485_1_pin3),
    .pin15(n7485_1_pin15), .pin14(n7485_1_pin3), .pin13(n7485_1_pin13), .pin12(n7485_1_pin12),
    .pin11(n7485_1_pin1), .pin10(n7485_1_pin10), .pin9(n7485_1_pin1));
  _7404 #(.VccGndPorts("true")) u_7404_2 (
    .pin7(n7404_2_pin7), .pin14(n7404_2_pin14), .pin13(dipswitch_1_sw1), .pin12(n7404_2_pin12));  // open: pin1, pin2, pin3, pin4, pin5, pin6, pin11, pin10, pin9, pin8
  _7400 #(.VccGndPorts("true")) u_7400_2 (
    .pin1(n7400_2_pin1), .pin2(n7400_2_pin2), .pin3(n7400_2_pin3), .pin7(n7404_1_pin7), .pin14(n7404_1_pin14));  // open: pin4, pin5, pin6, pin13, pin12, pin11, pin10, pin9, pin8
  _74138 #(.VccGndPorts("true")) u_74138_2 (
    .pin1(n74138_1_pin1), .pin2(n74138_1_pin2), .pin3(n74138_1_pin3), .pin4(n7404_1_pin6),
    .pin5(n7404_1_pin6), .pin6(n7404_1_pin5), .pin8(n7404_1_pin7), .pin16(n7404_1_pin14),
    .pin15(n7400_2_pin1), .pin14(n7400_2_pin2));  // open: pin7, pin13, pin12, pin11, pin10, pin9
  DipSwitch dipswitch_2 (
    .sw1(n7404_1_pin5), .sw2(n74138_1_pin3), .sw3(n74138_1_pin2), .sw4(n74138_1_pin1));  // open: sw5, sw6, sw7, sw8
  LED led_1 (.in(n7485_1_pin5));
  LED led_2 (.in(n74151_1_pin5));
  // DipSwitch dipswitch_3: pin names not known; wires that end beside it: n7485_1_pin15, n7485_1_pin13, n7485_1_pin12, n7485_1_pin10
  LED led_3 (.in(n7485_1_pin6));
  LED led_4 (.in(n7485_1_pin7));
  _7420 #(.VccGndPorts("true")) u_7420_2 (
    .pin1(n7404_2_pin14), .pin2(n7404_2_pin12), .pin4(n7400_1_pin6), .pin5(n7400_1_pin3),
    .pin6(n7420_2_pin6), .pin7(n7404_2_pin7), .pin14(n7404_2_pin14));  // open: pin3, pin13, pin12, pin11, pin10, pin9, pin8
  // DipSwitch dipswitch_4: pin names not known; wires that end beside it: n74151_1_pin9, n74151_1_pin10, n74151_1_pin11
  _7432 #(.VccGndPorts("true")) u_7432_1 (
    .pin1(n7420_1_pin6), .pin2(n7400_2_pin3), .pin3(n7432_1_pin3), .pin7(n7404_1_pin7), .pin14(n7404_1_pin14));  // open: pin4, pin5, pin6, pin13, pin12, pin11, pin10, pin9, pin8
  LED led_5 (.in(n7420_2_pin6));
  LED led_6 (.in(n7432_1_pin3));
  // also tied to GND on the sheet: {n7485_1_pin1, n74151_1_pin1, n7404_2_pin7, n7404_1_pin7}
  // also tied to VCC on the sheet: {n7404_1_pin14, n7485_1_pin3, n7404_2_pin14}
endmodule
