// Logisim project digital3.circ as structural Verilog: 1 circuit, main circuit main
module main (
);

  wire clock_1_out, d_ff_1_q, d_ff_1_qn, dipswitch_1_p1, dipswitch_1_p2, dipswitch_1_p3, dipswitch_2_p1,
       j_k_ff_1_q, j_k_ff_1_qn;

  // DipSwitch dipswitch_1: pin names not known; wires that end beside it: dipswitch_1_p1, dipswitch_1_p2, dipswitch_1_p3
  // DipSwitch dipswitch_2: pin names not known; wires that end beside it: dipswitch_2_p1
  J_K_Flip_Flop #(.trigger("falling")) j_k_ff_1 (
    .J(dipswitch_1_p1), .K(dipswitch_1_p2), .clk(dipswitch_1_p3), .Q(j_k_ff_1_q), .Qn(j_k_ff_1_qn),
    .preset(1'b0), .reset(1'b0));
  D_Flip_Flop d_ff_1 (.D(dipswitch_2_p1), .clk(clock_1_out), .Q(d_ff_1_q), .Qn(d_ff_1_qn), .preset(1'b0), .reset(1'b0));
  Clock clock_1 (.out(clock_1_out));
  LED led_1 (.in(j_k_ff_1_q));
  LED led_2 (.in(j_k_ff_1_qn));
  LED led_3 (.in(d_ff_1_q));
  LED led_4 (.in(d_ff_1_qn));
endmodule
