// Logisim project digital4.circ as structural Verilog: 1 circuit, main circuit main
module main (
);

  wire n7420_1_pin1, n7420_1_pin2, n7420_1_pin4, n7420_1_pin5, n7420_1_pin6, n7420_1_pin7, n7420_2_pin6,
       n7420_2_pin8, n74138_1_pin1, n74138_1_pin2, n74138_1_pin3, n74138_1_pin9, n74138_1_pin10,
       n74138_1_pin12, n74138_1_pin13, n74161_1_pin1, n74161_1_pin2, n74161_1_pin11;

  _7420 #(.ShowInternalStructure("true"), .VccGndPorts("true")) u_7420_1 (
    .pin1(n7420_1_pin1), .pin2(n7420_1_pin2), .pin4(n7420_1_pin4), .pin5(n7420_1_pin5), .pin6(n7420_1_pin6),
    .pin7(n7420_1_pin7), .pin14(n7420_1_pin4));  // open: pin3, pin13, pin12, pin11, pin10, pin9, pin8
  _74138 #(.ShowInternalStructure("true"), .VccGndPorts("true")) u_74138_1 (
    .pin1(n74138_1_pin1), .pin2(n74138_1_pin2), .pin3(n74138_1_pin3), .pin4(n7420_1_pin7),
    .pin5(n7420_1_pin7), .pin6(n7420_1_pin4), .pin7(n7420_1_pin5), .pin8(n7420_1_pin7), .pin16(n7420_1_pin4),
    .pin14(n7420_1_pin1), .pin13(n74138_1_pin13), .pin12(n74138_1_pin12), .pin11(n7420_1_pin2),
    .pin10(n74138_1_pin10), .pin9(n74138_1_pin9));  // open: pin15
  _74161 #(.ShowInternalStructure("true"), .VccGndPorts("true")) u_74161_1 (
    .pin1(n74161_1_pin1), .pin2(n74161_1_pin2), .pin3(n7420_1_pin7), .pin4(n7420_1_pin7),
    .pin5(n7420_1_pin7), .pin6(n7420_1_pin7), .pin7(n7420_1_pin4), .pin8(n7420_1_pin7), .pin16(n7420_1_pin4),
    .pin14(n74138_1_pin1), .pin13(n74138_1_pin2), .pin12(n74138_1_pin3), .pin11(n74161_1_pin11),
    .pin10(n7420_1_pin4), .pin9(n7420_1_pin4));  // open: pin15
  Clock clock_1 (.out(n74161_1_pin2));
  _7420 #(.ShowInternalStructure("true"), .VccGndPorts("true")) u_7420_2 (
    .pin1(n74138_1_pin12), .pin2(n7420_1_pin2), .pin4(n74138_1_pin10), .pin5(n7420_1_pin4),
    .pin6(n7420_2_pin6), .pin7(n7420_1_pin7), .pin14(n7420_1_pin4), .pin13(n74138_1_pin13),
    .pin12(n7420_1_pin2), .pin10(n7420_1_pin4), .pin9(n74138_1_pin9), .pin8(n7420_2_pin8));  // open: pin3, pin11
  _7404 #(.ShowInternalStructure("true"), .VccGndPorts("true")) u_7404_1 (
    .pin1(n74161_1_pin11), .pin2(n74161_1_pin1), .pin7(n7420_1_pin7), .pin14(n7420_1_pin4));  // open: pin3, pin4, pin5, pin6, pin13, pin12, pin11, pin10, pin9, pin8
  LED led_1 (.in(n7420_1_pin6));
  LED led_2 (.in(n7420_2_pin8));
  LED led_3 (.in(n7420_2_pin6));
  // also tied to GND on the sheet: n7420_1_pin7
  // also tied to VCC on the sheet: n7420_1_pin4
endmodule
