// Logisim project digital5.circ as structural Verilog: 1 circuit, main circuit main
module main (
);

  wire n7402_1_pin8, n7402_1_pin9, n7402_1_pin10, n7404_1_pin1, n7404_1_pin3, n7404_1_pin11, n7404_1_pin13,
       n7485_1_pin2, n7485_1_pin3, n7485_1_pin10, n7485_1_pin12, n7485_1_pin13, n7485_1_pin15, n74151_1_pin1,
       n74151_1_pin2, n74151_1_pin3, n74151_1_pin4, n74151_1_pin7, n74151_1_pin10, n74151_1_pin11,
       n74161_1_pin1, n74161_1_pin2, n74161_1_pin3, n74161_1_pin7, n74161_2_pin1, n74161_2_pin3,
       n74161_2_pin9, n74165_1_pin1, n74165_1_pin2, n74165_1_pin9, n74165_1_pin10, n74165_1_pin11,
       n74165_1_pin12, n74165_1_pin13, n74165_1_pin14, n74165_1_pin15, n74283_1_pin3, n74283_1_pin5,
       n74283_1_pin7, n74283_1_pin9, n74283_1_pin12, n74283_1_pin14;

  _74165 u_74165_1 (
    .pin1(n74165_1_pin1), .pin2(n74165_1_pin2), .pin15(n74165_1_pin15), .pin14(n74165_1_pin14),
    .pin13(n74165_1_pin13), .pin12(n74165_1_pin12), .pin11(n74165_1_pin11), .pin10(n74165_1_pin10),
    .pin9(n74165_1_pin9));  // open: pin3, pin4, pin5, pin6, pin7
  DipSwitch #(.number(3)) dipswitch_1 (.sw1(n74165_1_pin2), .sw2(n74165_1_pin1), .sw3(n74165_1_pin11));
  _7485 #(.ShowInternalStructure("true")) u_7485_1 (
    .pin1(n74165_1_pin12), .pin2(n7485_1_pin2), .pin3(n7485_1_pin3), .pin4(n7485_1_pin2),
    .pin15(n7485_1_pin15), .pin14(n74165_1_pin13), .pin13(n7485_1_pin13), .pin12(n7485_1_pin12),
    .pin11(n74165_1_pin14), .pin10(n7485_1_pin10), .pin9(n74165_1_pin15));  // open: pin5, pin6, pin7
  _7402 #(.ShowInternalStructure("true")) u_7402_1 (
    .pin10(n7402_1_pin10), .pin9(n7402_1_pin9), .pin8(n7402_1_pin8));  // open: pin1, pin2, pin3, pin4, pin5, pin6, pin13, pin12, pin11
  _74283 #(.ShowInternalStructure("true")) u_74283_1 (
    .pin2(n7485_1_pin12), .pin3(n74283_1_pin3), .pin5(n74283_1_pin5), .pin6(n7485_1_pin10),
    .pin7(n74283_1_pin7), .pin15(n7485_1_pin13), .pin14(n74283_1_pin14), .pin12(n74283_1_pin12),
    .pin11(n7485_1_pin15), .pin9(n74283_1_pin9));  // open: pin1, pin4, pin13, pin10
  _74161 #(.ShowInternalStructure("true")) u_74161_1 (
    .pin1(n74161_1_pin1), .pin2(n74161_1_pin2), .pin3(n74161_1_pin3), .pin4(n74161_1_pin3),
    .pin5(n74161_1_pin3), .pin6(n74161_1_pin3), .pin7(n74161_1_pin7), .pin15(n7402_1_pin9),
    .pin14(n7485_1_pin10), .pin13(n7485_1_pin12), .pin12(n7485_1_pin13), .pin11(n7485_1_pin15),
    .pin10(n74161_1_pin7), .pin9(n7402_1_pin10));
  DipSwitch #(.number(2)) dipswitch_2 (.sw1(n74161_1_pin1));  // open: sw2
  _7404 #(.ShowInternalStructure("true")) u_7404_1 (
    .pin1(n7404_1_pin1), .pin2(n74283_1_pin3), .pin3(n7404_1_pin3), .pin4(n74283_1_pin5),
    .pin13(n7404_1_pin13), .pin12(n74283_1_pin12), .pin11(n7404_1_pin11), .pin10(n74283_1_pin14));  // open: pin5, pin6, pin9, pin8
  _74151 #(.ShowInternalStructure("true")) u_74151_1 (
    .pin1(n74151_1_pin1), .pin2(n74151_1_pin2), .pin3(n74151_1_pin3), .pin4(n74151_1_pin4),
    .pin5(n74161_1_pin2), .pin7(n74151_1_pin7), .pin11(n74151_1_pin11), .pin10(n74151_1_pin10),
    .pin9(n74151_1_pin7));  // open: pin6, pin15, pin14, pin13, pin12
  _74161 #(.ShowInternalStructure("true")) u_74161_2 (
    .pin1(n74161_2_pin1), .pin2(n74151_1_pin4), .pin3(n74161_2_pin3), .pin4(n74161_2_pin3),
    .pin5(n74161_2_pin3), .pin6(n74161_2_pin3), .pin7(n74161_2_pin1), .pin14(n74151_1_pin3),
    .pin13(n74151_1_pin2), .pin12(n74151_1_pin1), .pin10(n74161_2_pin1), .pin9(n74161_2_pin9));  // open: pin15, pin11
  Clock clock_1 (.out(n74151_1_pin4));
  // DipSwitch #(.number(5)) dipswitch_3: pin names not known; wires that end beside it: n7404_1_pin13, n7404_1_pin11, n7404_1_pin1, n7404_1_pin3, n74283_1_pin7
  // DipSwitch #(.number(2)) dipswitch_4: pin names not known; wires that end beside it: n74151_1_pin11, n74151_1_pin10
  _7408 #(.ShowInternalStructure("true")) u_7408_1 (
    .pin1(n74283_1_pin7), .pin2(n74283_1_pin9), .pin3(n7402_1_pin8));  // open: pin4, pin5, pin6, pin13, pin12, pin11, pin10, pin9, pin8
  _7420 #(.ShowInternalStructure("true")) u_7420_1 (
    .pin1(n74161_2_pin1), .pin2(n74151_1_pin3), .pin4(n74151_1_pin2), .pin5(n74151_1_pin1),
    .pin6(n74161_2_pin9));  // open: pin3, pin13, pin12, pin11, pin10, pin9, pin8
  // also tied to GND on the sheet: {n74165_1_pin10, n7485_1_pin2, n74161_1_pin3, n74161_2_pin3, n74151_1_pin7}
  // also tied to VCC on the sheet: {n74165_1_pin9, n7485_1_pin3, n74161_1_pin7, n74161_2_pin1}
endmodule
